// Logisim project MultiCycleCPU.circ as structural Verilog: 4 circuits, main circuit ALU
module main (
  input  RAMUin,
  input  [7:0] DIN,
  input  Reset_Clock_on_Rising_Edge_for_Read_Write,
  input  ClearRAM,
  output out_5,
  output out_6,
  output out_7
);

  wire clock_1_out, control_logic_1_ain, control_logic_1_asen, control_logic_1_bin, control_logic_1_clear,
       control_logic_1_irin, control_logic_1_out_8, control_logic_1_out_9, control_logic_1_out_11,
       control_logic_1_out_14, control_logic_1_out_16, control_logic_1_out_18, control_logic_1_out_19,
       control_logic_1_r0, multiplexer_2_out, not_1_out;
  wire [1:0] control_logic_1_bout, counter_1_q;
  wire [2:0] control_logic_1_rout;
  wire [7:0] A_q, alu_1_output, B_q, counter_2_q, demultiplexer_1_out0, demultiplexer_1_out1,
       multiplexer_1_out, multiplexer_3_out, multiplexer_4_out, R0_2_q, R0_q, R1_q, R2_q, R3_q, R4_q, R5_q,
       R6_q, R7_q, ram_1_data;

  Clock clock_1 (.out(clock_1_out));
  Multiplexer #(.width(8), .enable("false")) multiplexer_1 (
    .in0(DIN), .in1(ram_1_data), .out(multiplexer_1_out), .sel(RAMUin));
  Demultiplexer #(.width(8), .enable("false")) demultiplexer_1 (
    .out0(demultiplexer_1_out0), .out1(demultiplexer_1_out1), .in(multiplexer_1_out),
    .sel(control_logic_1_irin));
  not not_1 (not_1_out, clock_1_out);
  Register R0 (.D(demultiplexer_1_out1), .en(control_logic_1_irin), .Q(R0_q), .clk(clock_1_out));  // open: clr
  Register R0_2 (.D(multiplexer_3_out), .en(control_logic_1_r0), .Q(R0_2_q), .clk(clock_1_out));  // open: clr
  Multiplexer #(.enable("false")) multiplexer_2 (.in0(1'b0), .in1(not_1_out), .out(multiplexer_2_out), .sel(out_5));
  Counter #(.width(2), .max('h3)) counter_1 (
    .Q(counter_1_q), .clk(clock_1_out), .clr(control_logic_1_clear));  // open: load, D, count, carry
  Register R1 (.D(multiplexer_3_out), .en(control_logic_1_out_8), .Q(R1_q), .clk(clock_1_out));  // open: clr
  Register R2 (.D(multiplexer_3_out), .en(control_logic_1_out_9), .Q(R2_q), .clk(clock_1_out));  // open: clr
  Multiplexer #(.select(2), .width(8), .enable("false")) multiplexer_3 (
    .in0(multiplexer_4_out), .in1(B_q), .in2(demultiplexer_1_out0), .out(multiplexer_3_out),
    .sel(control_logic_1_bout));  // open: in3
  Counter counter_2 (
    .Q(counter_2_q), .clk(multiplexer_2_out), .clr(Reset_Clock_on_Rising_Edge_for_Read_Write));  // open: load, D, count, carry
  Register R3 (.D(multiplexer_3_out), .en(control_logic_1_out_11), .Q(R3_q), .clk(clock_1_out));  // open: clr
  Multiplexer #(.select(3), .width(8), .enable("false")) multiplexer_4 (
    .in0(R0_2_q), .in1(R1_q), .in2(R2_q), .in3(R3_q), .in4(R4_q), .in5(R5_q), .in6(R6_q), .in7(R7_q),
    .out(multiplexer_4_out), .sel(control_logic_1_rout));
  Register R4 (.D(multiplexer_3_out), .en(control_logic_1_out_14), .Q(R4_q), .clk(clock_1_out));  // open: clr
  Register R5 (.D(multiplexer_3_out), .en(control_logic_1_out_16), .Q(R5_q), .clk(clock_1_out));  // open: clr
  RAM_part ram_1 (.addr(counter_2_q), .data(ram_1_data), .clk(multiplexer_2_out), .clr(ClearRAM));  // open: sel, ld
  Control_Logic control_logic_1 (
    .Ain(control_logic_1_ain), .Bin(control_logic_1_bin), .Bout(control_logic_1_bout[0]),
    .Asen(control_logic_1_asen), .DINout(control_logic_1_bout[1]), .Instruction(R0_q),
    .r0(control_logic_1_r0), .out_8(control_logic_1_out_8), .out_9(control_logic_1_out_9),
    .out_11(control_logic_1_out_11), .out_14(control_logic_1_out_14), .out_16(control_logic_1_out_16),
    .out_18(control_logic_1_out_18), .out_19(control_logic_1_out_19), .Rout(control_logic_1_rout),
    .in_3(counter_1_q), .IRin(control_logic_1_irin), .Clock(clock_1_out), .Clear(control_logic_1_clear),
    .Done(out_5));
  Register R6 (.D(multiplexer_3_out), .en(control_logic_1_out_18), .Q(R6_q), .clk(clock_1_out));  // open: clr
  Register R7 (.D(multiplexer_3_out), .en(control_logic_1_out_19), .Q(R7_q), .clk(clock_1_out));  // open: clr
  Register A (.D(multiplexer_3_out), .en(control_logic_1_ain), .Q(A_q), .clk(clock_1_out));  // open: clr
  ALU alu_1 (
    .A(A_q), .Asen(control_logic_1_asen), .B(multiplexer_3_out), .\output (alu_1_output), .Cout(out_6),
    .overflow_carrout(out_7));
  Register B (.D(alu_1_output), .en(control_logic_1_bin), .Q(B_q), .clk(clock_1_out));  // open: clr

  // Notes on the sheet:
  //   Bout
  //   DINout
  //   Ain
  //   Bin
  //   Asec
endmodule

module ALU (
  input  [7:0] A,
  input  Asen,
  input  [7:0] B,
  output [7:0] \output ,
  output overflow_carrout,
  output Cout
);

  wire adder_1_cout, adder_2_cout;
  wire [7:0] multiplexer_1_out, not_1_out;

  assign not_1_out = ~B;  // NOT_Gate not_1, 8 bits wide
  Multiplexer #(.width(8), .enable("false")) multiplexer_1 (
    .in0(B), .in1(not_1_out), .out(multiplexer_1_out), .sel(Asen));
  Multiplexer #(.enable("false")) multiplexer_2 (.in0(adder_2_cout), .in1(1'b0), .out(Cout), .sel(Asen));
  Adder #(.width(7)) adder_1 (
    .a(A[6:0]), .b(multiplexer_1_out[6:0]), .out(\output [6:0]), .cin(Asen), .cout(adder_1_cout));
  Adder #(.width(1)) adder_2 (
    .a(A[7]), .b(multiplexer_1_out[7]), .out(\output [7]), .cin(adder_1_cout), .cout(adder_2_cout));
  xor xor_1 (overflow_carrout, adder_1_cout, adder_2_cout);
endmodule

module Control_Logic (
  input  Clock,
  input  [7:0] Instruction,
  input  [1:0] in_3,
  output IRin,
  output Clear,
  output Done,
  output r0,
  output out_8,
  output out_9,
  output Ain,
  output out_11,
  output Bin,
  output Bout,
  output out_14,
  output Asen,
  output out_16,
  output DINout,
  output out_18,
  output out_19,
  output [2:0] Rout
);

  wire and_1_out, and_12_out, d_ff_1_qn, d_ff_2_q, decoder_1_out1, decoder_2_out0, decoder_2_out1,
       decoder_2_out2, decoder_2_out3, decoder_2_out4, decoder_2_out5, decoder_2_out6, decoder_2_out7,
       multiplexer_2_out, nor_1_out, not_1_out, not_2_out, or_1_out;
  wire [1:0] or_2_out;

  Decoder #(.select(2), .enable("false")) decoder_1 (
    .out0(Ain), .out1(decoder_1_out1), .out2(Bout), .sel(in_3));  // open: out3
  not not_1 (not_1_out, Instruction[7]);
  or or_1 (or_1_out, not_1_out, Bout);
  not not_2 (not_2_out, Instruction[7]);
  and and_1 (and_1_out, d_ff_1_qn, or_1_out);
  and and_2 (or_2_out[1], Instruction[7], Ain);
  nor nor_1 (nor_1_out, Instruction[7], Instruction[6]);
  not not_3 (Bin, Bout);
  and and_3 (DINout, not_2_out, Instruction[6]);
  or or_2 (or_2_out[0], nor_1_out, decoder_1_out1);
  D_Flip_Flop d_ff_1 (.clk(Clock), .D(and_1_out), .Q(Clear), .Qn(d_ff_1_qn));  // open: preset, en, reset
  Decoder #(.select(3), .enable("false")) decoder_2 (
    .out0(decoder_2_out0), .out1(decoder_2_out1), .out2(decoder_2_out2), .out3(decoder_2_out3),
    .out4(decoder_2_out4), .out5(decoder_2_out5), .out6(decoder_2_out6), .out7(decoder_2_out7),
    .sel(Instruction[5:3]));
  Multiplexer #(.select(2), .width(3), .enable("false")) multiplexer_1 (
    .in1(Instruction[2:0]), .in2(Instruction[5:3]), .out(Rout), .sel(or_2_out));  // open: in0, in3
  D_Flip_Flop d_ff_2 (.clk(Clock), .D(Clock), .Q(d_ff_2_q));  // open: Qn, preset, en, reset
  and and_4 (r0, and_1_out, decoder_2_out0);
  and and_5 (out_8, and_1_out, decoder_2_out1);
  and and_6 (out_9, and_1_out, decoder_2_out2);
  and and_7 (out_11, and_1_out, decoder_2_out3);
  and and_8 (out_14, and_1_out, decoder_2_out4);
  and and_9 (out_16, and_1_out, decoder_2_out5);
  and and_10 (out_18, and_1_out, decoder_2_out6);
  and and_11 (out_19, and_1_out, decoder_2_out7);
  Multiplexer #(.select(2), .enable("false")) multiplexer_2 (
    .in0(1'b0), .in1(1'b1), .in2(1'b0), .in3(1'b0), .out(multiplexer_2_out), .sel(Instruction[7:6]));
  and and_12 (and_12_out, d_ff_2_q, multiplexer_2_out);
  Multiplexer #(.enable("false")) multiplexer_3 (.in0(and_1_out), .in1(and_12_out), .out(Done), .sel(and_12_out));

  assign Asen = Instruction[6];
  assign IRin = Clear;

  // Notes on the sheet:
  //   Rxin
  //   Rxout
  //   Ryout
endmodule

// RAMU
module RAM (
  input  [7:0] Data_Store,
  input  Store,
  input  Clk,
  input  Reset_Clock_on_Rising_Edge_for_Read_Write,
  input  ClearRAM,
  output [7:0] Output
);

  wire not_1_out;
  wire [7:0] counter_1_q;

  Counter counter_1 (
    .Q(counter_1_q), .clk(Clk), .clr(Reset_Clock_on_Rising_Edge_for_Read_Write));  // open: load, D, count, carry
  assign Output = Store ? Data_Store : 8'bz;  // Controlled_Buffer controlled_buffer_1
  not not_1 (not_1_out, Store);
  RAM_part ram_1 (.addr(counter_1_q), .data(Output), .clk(Clk), .ld(not_1_out), .clr(ClearRAM));  // open: sel
endmodule
